# Fritzing sketch microcontroller HAM radio 20m QRP (saved by Fritzing 0.9.3b)
breadboards: 3

parts:
  M1 = ESP32-S3-DevKitC-1-N8R8-v1 [part_number=ESP32-S3-DevKitC-1-N8R8-v1]
  Bauteil1 = Adafruit Si5351A Clock Generator [part_number="Adafruit #2045"]  # not connected
  SW1 = ENCODER_RGB_CA [package=encoder_led_3]  # not connected
  U1 = SD_CARD_SOCKET [package=sdcard_4uconn]  # not connected
  TRS1 = Audio Jack (TRS) 3.5mm [package="4Ucon 08780 [THT]"]  # not connected
  LCD1 = TFT 3.5 inch 480x320 w touch and SD  # not connected

nets:
  N1: M1.pin_1, M1.pin_2
  N2: M1.pin_22, M1.pin_23, M1.pin_24, M1.pin_44

custom parts:
  ESP32-S3-DevKitC-1-N8R8-v1: ESP32-S3-DevKitC-1-N8R8-v1 This module is 44pins long (2x22) and 11 pins width.
  Adafruit Si5351A Clock Generator: Never hunt around for another crystal again, with the Si5351A clock generator breakout from Adafruit! This chip has a precision 25MHz crystal reference and internal PLL and dividers so it can generate just about any frequency, from <8KHz up to 150+ MHz. The Si5351A clock generator is an I2C controller clock generator. It uses the onboard precision clock to drive multiple PLL's and clock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
  TFT 3.5 inch 480x320 w touch and SD: This is a generic 1.8 tft spi lcd display available on ebay and others. The 1.8"3.5 inch 480X320 SPI TFT Module 320x480 LCD Display - Touch.
